# Fritzing sketch 土壤檢測器 (saved by Fritzing 0.9.3b)
breadboards: 1

parts:
  元件2 = DHT22 module
  元件3 = Soil Moisture Sensor
  元件4 = Arduino Uno (Rev3)
  元件5 = Real Time Clock Module - DS1307 RTC Breakout Board
  KY-2 = Keyes Relay [package=THT]
  KY-3 = Keyes Relay [package=THT]
  J1 = Piezo Speaker  # not connected
  J3 = Piezo Speaker
  J2 = Piezo Speaker

nets:
  VCC: 元件2.VCC, 元件3.VCC, 元件4.5V, 元件5.5V, KY-2.power, KY-3.power
  GND: 元件2.GND, 元件3.GND, 元件4.GND, 元件5.GND
  N1: 元件2.DATA, 元件4.D3_PWM
  N2: 元件3.SIG, 元件4.A0
  N3: 元件4.D10_PWM/SS, KY-3.signal
  N4: 元件4.D11_PWM/MOSI, KY-2.signal
  N5: 元件4.D5_PWM, 元件5.SQW
  N6: 元件4.D6_PWM, 元件5.SCL
  N7: 元件4.D7, 元件5.SDA
  N8: KY-2.ground, KY-3.ground
  N9: KY-2.C, KY-3.C, J3.pin2
  N10: KY-2.NO, J2.pin2

custom parts:
  Real Time Clock Module - DS1307 RTC Breakout Board: This a custom designed module for the DS1307 Real Time Clock. The module comes fully assembled and pre-programmed with the current time (ok, so it's our current time - MST). The included Lithium coin cell battery (CR1225 41mAh) will run the module for a minimum of 9 years (17 years typical) without external 5V power. The DS1307 is accessed via the I2C protocol. We've written a test-bed to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
  Keyes Relay: The Keyes 5V relay module is suitable for SCM development, home appliance control. It uses a 5V~12V TIL control signal which can control DC / AC signal.
